# Fritzing sketch fader - l293d - arduino uno (saved by Fritzing 0.8.0b)
breadboards: 1

parts:
  Arduino1 = Arduino
  IC1 = L293D [package=THT]
  Fader_motor = DC Motor
  Fader_position_pot = Slide Potentiometer
  Fader_touch_sensor = Ceramic Disk Capacitor [package=THT]
  R1 = 1M Ω Resistor [package=THT]
  SetPoint = Rotary Potentiometer (Large) [maximum_resistance=100kΩ package=THT]

nets:
  N1: Arduino1.D10, IC1.In_1
  N2: Arduino1.D9, IC1.In_2
  N3: Arduino1.D4, R1.Pin_1
  N4: Arduino1.D2, Fader_touch_sensor.pin_1, R1.Pin_0
  N5: Arduino1.+5V, IC1.Enable_1, IC1.+V, Fader_position_pot.leg1, SetPoint.leg1
  N6: Arduino1.GND, IC1.0V, Fader_position_pot.leg2, Fader_touch_sensor.pin_0, SetPoint.leg2
  N7: Arduino1.VIN, IC1.+Vmotor
  N8: Arduino1.A0, SetPoint.wiper
  N9: Arduino1.A3, Fader_position_pot.wiper
  N10: IC1.Out_1_(_Controlled_by_Enable_1_), Fader_motor.pin_2
  N11: IC1.Out_2_(_Controlled_by_Enable_1_), Fader_motor.pin_1
