# Fritzing sketch fader - tlc5940 - l293d - arduino uno (saved by Fritzing 0.8.7b)
breadboards: 1

parts:
  Arduino2 = Arduino Uno (Rev3)
  IC3 = DIP - 28 pins [chip_label=TLC5940 package="DIP (Dual Inline) [THT]"]
  R4 = Resistor [tolerance=±5% resistance=2.2k package=THT]
  R5 = Resistor [tolerance=±5% resistance=10k package=THT]
  IC4 = L293D [package=THT]
  Fader_motor1 = DC Motor
  Fader_position_pot1 = Slide Potentiometer [maximum_resistance=100kΩ]
  Fader_touch_sensor1 = Ceramic Capacitor [capacitance=100nF package="200 mil [THT, multilayer]"]
  R6 = Resistor [tolerance=±5% resistance=1M package=THT]
  SetPoint1 = Rotary Potentiometer (Large) [maximum_resistance=100kΩ package=THT]

nets:
  N1: Arduino2.A0, SetPoint1.wiper
  N2: Arduino2.A3, Fader_position_pot1.wiper
  N3: Arduino2.GND, IC3.pin22, IC3.pin27, R4.Pin_0, IC4.0V, Fader_position_pot1.leg2, SetPoint1.leg2
  N4: Arduino2.D2, Fader_touch_sensor1.1, R6.Pin_0
  N5: Arduino2.D4, R6.Pin_1
  N6: Arduino2.VIN, IC4.+Vmotor
  N7: IC3.pin1, IC4.In_1
  N8: IC3.pin19, IC3.pin21, R5.Pin_0, IC4.Enable_1, IC4.+V, Fader_position_pot1.leg1, SetPoint1.leg1
  N9: IC3.pin20, R4.Pin_1
  N10: IC3.pin23, R5.Pin_1
  N11: IC3.pin28, IC4.In_2
  N12: IC4.Out_1_(_Controlled_by_Enable_1_), Fader_motor1.pin_2
  N13: IC4.Out_2_(_Controlled_by_Enable_1_), Fader_motor1.pin_1

custom parts:
  DIP - 28 pins: A DIP stand-in part for whatever IC you want. With 28 pins on a 300mil dual inline package (DIP) footprint.
