# Fritzing sketch fader - tlc5940 - l293d - arduino due (saved by Fritzing 0.8.7b)
breadboards: 1

parts:
  IC1 = L293D [package=THT]
  Fader_motor = DC Motor
  SetPoint = Rotary Potentiometer (Large) [maximum_resistance=100kΩ package=THT]
  IC2 = DIP - 28 pins [chip_label=TLC5940 package="DIP (Dual Inline) [THT]"]
  R2 = Resistor [tolerance=±5% resistance=2.2k package=THT]
  R3 = Resistor [tolerance=±5% resistance=10k package=THT]
  Fader_position_pot = Slide Potentiometer [maximum_resistance=100kΩ]
  Fader_touch_sensor = Ceramic Capacitor [capacitance=100nF package="200 mil [THT, multilayer]"]
  Parte1 = Arduino Due (Rev2b)
  VCC1 = Battery block 9V
  C1 = Electrolytic Capacitor [capacitance=0.47mF package="100 mil [THT, electrolytic]"]

nets:
  5V: IC1.Enable_1, IC1.+V, SetPoint.leg1, IC2.pin19, IC2.pin21, R2.Pin_0, Fader_position_pot.leg1, Parte1.5V
  N1: IC1.In_1, IC2.pin1
  N2: IC1.Out_1_(_Controlled_by_Enable_1_), Fader_motor.pin_1, C1.+
  GND: IC1.0V, SetPoint.leg2, IC2.pin22, IC2.pin27, R3.Pin_0, Fader_position_pot.leg2, Parte1.GND, VCC1.-
  N3: IC1.Out_2_(_Controlled_by_Enable_1_), Fader_motor.pin_2, C1.-
  N4: IC1.In_2, IC2.pin28
  9V: IC1.+Vmotor, VCC1.+
  N5: SetPoint.wiper, Parte1.A6
  GSCLK: IC2.pin18, Parte1.D11_PWM
  N6: IC2.pin20, R3.Pin_1
  BLANK: IC2.pin23, R2.Pin_1, Parte1.D9_PWM
  XLAT: IC2.pin24, Parte1.D10_PWM/SS0
  SCLK: IC2.pin25, Parte1.SDA1
  SIN: IC2.pin26, Parte1.D18/TX1
  N7: Fader_position_pot.wiper, Parte1.A9
  TOUCH PIN: Fader_touch_sensor.1, Parte1.D2_PWM

custom parts:
  DIP - 28 pins: A DIP stand-in part for whatever IC you want. With 28 pins on a 300mil dual inline package (DIP) footprint.
