# Fritzing sketch motorfader (saved by Fritzing 0.7.4b)
breadboards: 1

parts:
  S1 = Pushbutton [package="[THT]"]
  U1 = Arduino Mega
  M1 = DC Motor
  IC1 = L293D [package=THT]
  R1 = Slide Potentiometer [maximum_resistance=100kΩ]  # not connected
  R2 = Resistor [tolerance=±5% resistance=10k package=THT]
  C1 = Electrolytic Capacitor [capacitance=10µF voltage=50V package="100 mil [THT, electrolytic]"]
  M2 = DC Motor
  R3 = Slide Potentiometer [maximum_resistance=100kΩ]  # not connected
  R4 = Rotary Potentiometer (Small) [maximum_resistance=100kΩ]  # not connected

nets:
  N1: S1.Pin_1, S1.Pin_2, U1.D22, R2.Pin_0
  N2: S1.Pin_3, S1.Pin_4, U1.+5V
  N3: U1.GND, IC1.0V, R2.Pin_1, C1.-
  N4: U1.VIN, IC1.+Vmotor, IC1.+V, C1.+
  N5: U1.D24, U1.D34, IC1.Enable_1, IC1.In_2
  N6: U1.D26, IC1.In_1
  N7: U1.D28, IC1.In_4
  N8: U1.D30, IC1.In_3
  N9: U1.D32, IC1.Enable_2
  N10: M1.pin_1, IC1.Out_2_(_Controlled_by_Enable_1_)
  N11: M1.pin_2, IC1.Out_1_(_Controlled_by_Enable_1_)
  N12: IC1.Out_3_(_Controlled_by_Enable_2_), M2.pin_1
  N13: IC1.Out_4_(_Controlled_by_Enable_2_), M2.pin_2
